# Fritzing sketch Electrical Components (saved by Fritzing 0.9.2b)

parts:
  920KV_Motor1 = DJI 920 KV Motor
  920KV_Motor2 = DJI 920 KV Motor
  920KV_Motor3 = DJI 920 KV Motor
  920KV_Motor4 = DJI 920 KV Motor
  Mod1 = Raspberry Pi 4B  # not connected
  M1 = ESC
  M2 = ESC
  M3 = ESC
  M4 = ESC
  IC1 = Rasberry Pi NIOR Camera [chip_label=IC package="DIP (Dual Inline) [THT]"]  # not connected
  U1 = LIPO-2000mAh [package=lipo-2000]  # not connected
  U2 = SUP500F [package=sup500f]  # not connected

nets:
  N1: 920KV_Motor1.w, M1.W
  N2: 920KV_Motor1.v, M1.V
  N3: 920KV_Motor1.u, M1.U
  N4: 920KV_Motor2.w, M2.W
  N5: 920KV_Motor2.v, M2.V
  N6: 920KV_Motor2.u, M2.U
  N7: 920KV_Motor3.w, M4.W
  N8: 920KV_Motor3.v, M4.V
  N9: 920KV_Motor3.u, M4.U
  N10: 920KV_Motor4.w, M3.W
  N11: 920KV_Motor4.v, M3.V
  N12: 920KV_Motor4.u, M3.U
  GND: M1.GND, M4.GND
  5V: M1.5V, M4.5V
  GND_2: M2.GND, M3.GND
  5V_2: M2.5V, M3.5V

custom parts:
  DJI 920 KV Motor: DJI Brushless Outrunner 2212/920K Motor F330-550
  Rasberry Pi NIOR Camera: Camera
